# Fritzing sketch PI_UNO (saved by Fritzing 0.9.3b)
breadboards: 1

parts:
  Raspberry_Pi_1 = Raspberry Pi 3 [part_number=RPI-3-V1.2]
  Arduino_uno = Arduino Uno (Rev3) - ICSP
  R1 = Resistor [tolerance=±5% resistance=1k package="0603 [SMD]"]
  R2 = Resistor [tolerance=±5% resistance=2.2k package="0603 [SMD]"]

nets:
  GND: Raspberry_Pi_1.GND, Arduino_uno.GND, R2.Pin_0
  N1: Raspberry_Pi_1.GPIO15, R1.Pin_0, R2.Pin_1
  N2: Raspberry_Pi_1.GPIO14, Arduino_uno.D0/RX
  N3: Arduino_uno.D1/TX, R1.Pin_1
